// Logisim project TP5-6.circ as structural Verilog: 4 circuits, main circuit SYSTEM
module SYSTEM (
  input  Rst
);

  wire and_1_out, Clavier_p9, Clavier_p10, Clk, clr_in, clr_out, CS_CON, CS_KEY, hit, IO_ACK, IORD_REQ,
       IOWR_REQ, PORT_ID_KEY, read, undriven, write;
  wire [6:0] char, key;
  wire [31:0] bit_extender_1_out, bit_extender_2_out, IO_ADDR, IO_DIN, IO_DOUT, multiplexer_1_out, undriven_2;

  Clock u_clk (.out(Clk));
  // Nios2Simulator nios2simulator_1: pin names not known; wires that end beside it: Clk, Rst, IO_ACK, {32{1'b0}}, 1'b0
  Keyboard keyboard_1 (.clk(Clk), .re(read), .clr(clr_in), .avail(hit), .data(key));
  TTY tty_1 (.data(char), .clk(Clk), .we(write), .clr(clr_out));
  RAM #(.addrWidth(16), .dataWidth(32)) RAM_1 (.clr(IO_ADDR[2]));  // open: addr, data, sel, clk, ld
  // FSM_Entity #(.content("state_machine example @[50,50,800,500]{\n	in CS_CONSOLE[1]   @[50,100,85,15];IOWR_REQ[1]   @[50,141,68,15];\n	out write[1]   @[814,140,36,15];IO_ACK[1]   @[803,257,47,15];\n	codeWidth = 2;\n	reset = S0;\n	\n	state S0[\"00\"]:\n	 	@[382,407,30,30]\n		set write=\"0\";IO_ACK=\"0\";  @[382,407,30,30]	\n		goto S1  when (CS_CONSOLE.IOWR_REQ)   @[394,350,161,21]; \n	state S1[\"01\"]:\n	 	@[386,251,30,30]\n		set write=\"1\";IO_ACK=\"1\";  @[386,251,30,30]	\n		goto S2  when default   @[390,220,50,21]; \n	state S2[\"10\"]:\n	 	@[379,130,30,30]\n		set write=\"0\";IO_ACK=\"1\";  @[379,130,30,30]	\n		goto S0  when default   @[283,287,50,21]; \n}")) Console: pin names not known; wires that end beside it: Clk, Rst, IORD_REQ, IOWR_REQ, IO_ACK
  // FSM_Entity #(.content("state_machine example @[50,50,800,500]{\n	in CS_KEY[1]   @[50,100,50,15];IORD_REQ[1]   @[50,147,66,15];PORT_ID_KEY[1]   @[50,192,84,15];\n	out IO_ACK[1]   @[803,140,47,15];read[1]   @[815,170,35,15];\n	codeWidth = 2;\n	reset = S0;\n	\n	state S0[\"00\"]:\n	 	@[401,135,30,30]\n		set read=\"0\";IO_ACK=\"0\";  @[401,135,30,30]	\n		goto S1  when (IORD_REQ.CS_KEY)   @[403,253,124,21]; \n	state S1[\"01\"]:\n	 	@[326,298,30,30]\n		set read=(/PORT_ID_KEY);IO_ACK=\"1\";  @[326,298,30,30]	\n		goto S2  when default   @[239,287,50,21]; \n	state S2[\"10\"]:\n	 	@[200,183,30,30]\n		set read=\"0\";IO_ACK=\"1\";  @[200,183,30,30]	\n		goto S0  when default   @[278,125,50,21]; \n}")) Clavier: pin names not known; wires that end beside it: CS_CON, IOWR_REQ, Clk, Rst, CS_KEY, IORD_REQ, PORT_ID_KEY, write, Clavier_p9, Clavier_p10, read
  assign IO_DIN = undriven ? undriven_2 : 32'bz;  // Controlled_Buffer controlled_buffer_1
  // Probe on IO_ADDR
  // Probe on IO_DOUT
  // Probe on IO_DIN
  detect_char detect_char_1 (.in_1(IO_DOUT), .char(char), .clear(clr_out));
  or or_1 (IO_ACK, Clavier_p9, Clavier_p10);
  console_decodage console_decodage_1 (.in_1(IO_ADDR), .CS_CON(CS_CON));
  assign IO_DIN = and_1_out ? multiplexer_1_out : 32'bz;  // Controlled_Buffer controlled_buffer_2
  and and_1 (and_1_out, IORD_REQ, CS_KEY);
  clavier_decodage clavier_decodage_1 (.in_1(IO_ADDR), .PORT_ID_KEY(PORT_ID_KEY), .CS_KEY(CS_KEY));
  assign bit_extender_1_out = {{25{1'b0}}, key};  // Bit_Extender bit_extender_1
  Multiplexer #(.width(32), .enable("false")) multiplexer_1 (
    .in0(bit_extender_1_out), .in1(bit_extender_2_out), .out(multiplexer_1_out), .sel(PORT_ID_KEY));
  assign bit_extender_2_out = {{31{1'b0}}, hit};  // Bit_Extender bit_extender_2
  // Pins of 1 and 16 bits meet at IO_ADDR[17:2]

  // Notes on the sheet:
  //   TP 5-6 : entrées/sorties bus
  //   Processeur NIOS
  //   Périphérique clavier
  //   contents of RAM_1 (hex, n*v repeats v):
  //   1004004 380 3ffd26 107883a 19000007 deffff04 20000626 dfc00015 700 dfc00017 dec00104 18c00044 3ff726
  //   f800283a 1800284 540 11800326 1009883a 700 3ffb26 f800283a 1e00074 39ffc004 39400137 283ffe26
  //   39400037 2805883a f800283a 1e00034 39dc1004 39000025 f800283a a00034 109c1004 1000034 21002004
  //   11000025 f800283a 26*0 6c6c6548 6f77206f a646c72 0 4f494e20 49492053 6f727020 73736563 a726f 0 0 0
  //   3f 6 5b 4f 66 6d 7d 7 7f 6f 77 7c 39 5e 79 71 65439*0 30 30 8 8 8
  //   Périphérique console
endmodule

module console_decodage (
  input  [31:0] in_1,
  output CS_CON
);

  and and_1 (CS_CON, ~in_1[2], ~in_1[3], ~in_1[4], ~in_1[5], in_1[6], ~in_1[7], ~in_1[8], ~in_1[9], ~in_1[10], ~in_1[11], in_1[12], in_1[13], in_1[14], ~in_1[15], ~in_1[16], ~in_1[17], ~in_1[18], ~in_1[19], ~in_1[20], ~in_1[21], ~in_1[22], ~in_1[23], ~in_1[24], ~in_1[25], ~in_1[26], ~in_1[27], ~in_1[28], ~in_1[29], ~in_1[30], in_1[31]);  // AND_Gate
endmodule

module detect_char (
  input  [31:0] in_1,
  output [6:0] char,
  output clear
);


  assign char = in_1[6:0];
  assign clear = in_1[7];
endmodule

module clavier_decodage (
  input  [31:0] in_1,
  output PORT_ID_KEY,
  output CS_KEY
);

  and and_1 (CS_KEY, ~in_1[3], ~in_1[4], ~in_1[5], ~in_1[6], ~in_1[7], in_1[8], in_1[9], in_1[10], in_1[11], in_1[12], in_1[13], in_1[14], in_1[15], ~in_1[16], ~in_1[17], ~in_1[18], ~in_1[19], ~in_1[20], ~in_1[21], ~in_1[22], ~in_1[23], ~in_1[24], ~in_1[25], ~in_1[26], ~in_1[27], ~in_1[28], ~in_1[29], ~in_1[30], in_1[31]);  // AND_Gate

  assign PORT_ID_KEY = in_1[2];
endmodule
